# Fritzing sketch circuitry (saved by Fritzing 0.9.3b)
breadboards: 1

parts:
  T-Cobbler1 = T-Cobbler
  module1 = RGB LED
  module17 = PCF8591
  module18 = Analog Temperature

nets:
  N1: T-Cobbler1.3V3#0, module1.VCC
  N2: T-Cobbler1.SDA1, module17.SDA
  N3: T-Cobbler1.SCL1, module17.SCL
  N4: T-Cobbler1.GPIO17, module18.DO
  N5: T-Cobbler1.3V3#8, module18.VCC
  N6: T-Cobbler1.GND#12, module18.GND
  N7: T-Cobbler1.GPIO5, module1.B
  N8: T-Cobbler1.GPIO6, module1.G
  N9: T-Cobbler1.GPIO13, module1.R
  N10: T-Cobbler1.GND#19, module17.GND
  N11: module17.AIN0, module18.AO

custom parts:
  T-Cobbler: T-Cobbler for RPi B+ and Rpi2 from SunFounder
  RGB LED: RGB LED module of SunFounder Sensor Kit
  PCF8591: PCF8591 ADC module for SunFounder Sensor Kit
  Analog Temperature: Analog Temperature module of SunFounder Sensor Kit
